# Fritzing sketch RandomNumberBlock (saved by Fritzing 0.9.2b)
breadboards: 1

parts:
  VCC_6F22 = Battery block 9V
  Motherboard = Arduino Nano (Rev3.0)
  Button = Pushbutton [package=THT]
  S_Master = Toggle Switch [package=THT]
  Digitron = 7-SEGMENT-4DIGIT-YOUNGSUN [package=7-segment-4digit-youngsun-longpads]
  Sound_Sensor = Grove Buzz

nets:
  GND: VCC_6F22.-, Motherboard.GND, Button.leg1, Digitron.GND, Sound_Sensor.GND
  N1: VCC_6F22.+, S_Master.COM
  N2: Motherboard.D2, Button.leg0
  N3: Motherboard.D4, Digitron.DIO
  N4: Motherboard.D5, Digitron.RCLK
  N5: Motherboard.D6, Digitron.SCLK
  N6: Motherboard.VIN, S_Master.L2
  VCC: Motherboard.5V, Digitron.VCC, Sound_Sensor.VCC
  N7: Motherboard.A0, Sound_Sensor.AO

custom parts:
  7-SEGMENT-4DIGIT-YOUNGSUN: This is a part for the 4-Digit 7-segment LEDs from Young Sun. Different from the Digikey LEDs, all 16 pins are used. The LONGPADS Variant is used for a test jig, but you may like it because there is more pad to solder to. If you are concerned about routing space, the standard works just fine though.
  Grove Buzz: A buzz
